// Logisim project CRC.circ as structural Verilog: 2 circuits, main circuit CRC
module CRC (
  input  [7:0] A,
  input  [3:0] B,
  output [10:0] C
);

  wire mod2_4bit_1_d, mod2_4bit_2_d, mod2_4bit_3_d, mod2_4bit_4_d, mod2_4bit_5_d, mod2_4bit_6_d,
       mod2_4bit_7_d, mod2_4bit_8_d;
  wire [2:0] mod2_4bit_1_c, mod2_4bit_2_c, mod2_4bit_3_c, mod2_4bit_4_c, mod2_4bit_5_c, mod2_4bit_6_c,
       mod2_4bit_7_c;

  mod2_4bit mod2_4bit_1 (.A(A[7:4]), .B(B), .C(mod2_4bit_1_c), .D(mod2_4bit_1_d));
  mod2_4bit mod2_4bit_2 (.A({mod2_4bit_1_c, A[3]}), .B(B), .C(mod2_4bit_2_c), .D(mod2_4bit_2_d));
  mod2_4bit mod2_4bit_3 (.A({mod2_4bit_2_c, A[2]}), .B(B), .C(mod2_4bit_3_c), .D(mod2_4bit_3_d));
  mod2_4bit mod2_4bit_4 (.A({mod2_4bit_3_c, A[1]}), .B(B), .C(mod2_4bit_4_c), .D(mod2_4bit_4_d));
  mod2_4bit mod2_4bit_5 (.A({mod2_4bit_4_c, A[0]}), .B(B), .C(mod2_4bit_5_c), .D(mod2_4bit_5_d));
  mod2_4bit mod2_4bit_6 (.A({mod2_4bit_5_c, 1'b0}), .B(B), .C(mod2_4bit_6_c), .D(mod2_4bit_6_d));
  mod2_4bit mod2_4bit_7 (.A({mod2_4bit_6_c, 1'b0}), .B(B), .C(mod2_4bit_7_c), .D(mod2_4bit_7_d));
  mod2_4bit mod2_4bit_8 (.A({mod2_4bit_7_c, 1'b0}), .B(B), .C(C[2:0]), .D(mod2_4bit_8_d));

  assign C[10:3] = A;
endmodule

module mod2_4bit (
  input  [3:0] A,
  input  [3:0] B,
  output [2:0] C,
  output D
);

  wire xor_4_out;
  wire [2:0] xor_1_out;

  xor xor_1 (xor_1_out[0], A[0], B[0]);
  xor xor_2 (xor_1_out[1], A[1], B[1]);
  xor xor_3 (xor_1_out[2], A[2], B[2]);
  xor xor_4 (xor_4_out, A[3], B[3]);
  Multiplexer #(.width(3)) multiplexer_1 (.in0(A[2:0]), .in1(xor_1_out), .out(C), .sel(A[3]));  // open: en

  assign D = A[3];
endmodule
