// Logisim project FSM.circ as structural Verilog: 4 circuits, main circuit fsm
module fsm (
  input  CLR,
  input  [1:0] In,
  output Z
);

  wire CLK_out;
  wire [2:0] register_1_q, reset_1_next_status, status_trans_1_out_3;

  status_trans status_trans_1 (.status(register_1_q), .in(In), .out_3(status_trans_1_out_3));
  reset reset_1 (.s(status_trans_1_out_3), .clear(CLR), .next_status(reset_1_next_status));
  Register #(.width(3)) register_1 (.D(reset_1_next_status), .Q(register_1_q), .clk(CLK_out));  // open: en, clr
  Clock CLK (.out(CLK_out));
  \output  output_1 (.status(register_1_q), .in(In), .z(Z));
endmodule

module \output  (
  input  [2:0] status,
  input  [1:0] in,
  output z
);

  wire not_1_out, not_2_out;

  not not_1 (not_1_out, status[2]);
  not not_2 (not_2_out, in[0]);
  and and_1 (z, status[0], status[1], not_1_out, not_2_out);
endmodule

module reset (
  input  [2:0] s,
  input  clear,
  output [2:0] next_status
);

  Multiplexer #(.width(3)) multiplexer_1 (.in0(s), .in1(3'b000), .out(next_status), .sel(clear));  // open: en
endmodule

module status_trans (
  input  [2:0] status,
  input  [1:0] in,
  output [2:0] out_3
);

  wire and_2_out, and_3_out, and_4_out, and_5_out, and_6_out, and_7_out, and_8_out, and_9_out, not_1_out,
       not_2_out, not_3_out, not_4_out, not_5_out, not_6_out, not_7_out, not_8_out, not_9_out, not_10_out,
       not_11_out, not_12_out, not_13_out, not_14_out, not_15_out, not_16_out, not_17_out;

  not not_1 (not_1_out, in[0]);
  not not_2 (not_2_out, status[1]);
  not not_3 (not_3_out, in[1]);
  not not_4 (not_4_out, status[1]);
  not not_5 (not_5_out, in[0]);
  not not_6 (not_6_out, status[0]);
  not not_7 (not_7_out, in[1]);
  not not_8 (not_8_out, status[0]);
  not not_9 (not_9_out, in[0]);
  not not_10 (not_10_out, status[1]);
  not not_11 (not_11_out, status[0]);
  not not_12 (not_12_out, in[1]);
  not not_13 (not_13_out, status[1]);
  not not_14 (not_14_out, in[0]);
  not not_15 (not_15_out, status[0]);
  not not_16 (not_16_out, in[0]);
  not not_17 (not_17_out, in[1]);
  and and_1 (out_3[2], status[1], status[0], not_1_out);
  and and_2 (and_2_out, not_2_out, status[0], not_3_out);
  and and_3 (and_3_out, not_4_out, status[0], not_5_out);
  and and_4 (and_4_out, status[1], not_6_out, not_7_out);
  and and_5 (and_5_out, status[1], not_8_out, not_9_out);
  and and_6 (and_6_out, not_10_out, not_11_out, not_12_out, in[0]);
  and and_7 (and_7_out, not_13_out, status[0], not_14_out);
  and and_8 (and_8_out, status[1], not_15_out, not_16_out);
  and and_9 (and_9_out, status[1], status[0], not_17_out, in[0]);
  or or_1 (out_3[1], and_2_out, and_3_out, and_4_out, and_5_out);
  or or_2 (out_3[0], and_6_out, and_7_out, and_8_out, and_9_out);
endmodule
