// Logisim project FtoI.circ as structural Verilog: 3 circuits, main circuit ftoi
module ftoi (
  input  [15:0] float,
  output [31:0] \int 
);

  wire [1:0] branch;
  wire [31:0] nomorlized;

  normolized normolized_1 (.fraction(float[9:0]), .exponent(float[14:10]), .sign(float[15]), .out_4(nomorlized));
  select select_1 (.exponent(float[14:10]), .branch(branch));
  Multiplexer #(.select(2), .width(32)) multiplexer_1 (
    .in0(nomorlized), .in1({32{1'b0}}), .in2({32{1'b0}}), .in3({32{1'b0}}), .out(\int ), .sel(branch));  // open: en

  // Other names for the same wires on the sheet: exponent[4:0] = float[14:10]; sign = float[15];
  //   fraction[9:0] = float[9:0]
endmodule

module select (
  input  [4:0] exponent,
  output [1:0] branch
);

  Comparator #(.width(5)) comparator_1 (.a(exponent), .b({5{1'b0}}), .eq(branch[0]));  // open: gt, lt
  Comparator #(.width(5)) comparator_2 (.a(exponent), .b({5{1'b1}}), .eq(branch[1]));  // open: gt, lt
endmodule

module normolized (
  input  [9:0] fraction,
  input  [4:0] exponent,
  input  sign,
  output [31:0] out_4
);

  wire comparator_1_lt;
  wire [4:0] subtractor_1_out;
  wire [31:0] bit_extender_1_out, multiplexer_1_out, shifter_1_out, shifter_2_out, subtractor_2_out;

  assign bit_extender_1_out = {{21{1'b0}}, {1'b1, fraction}};  // Bit_Extender bit_extender_1
  Subtractor #(.width(5)) subtractor_1 (.a(exponent), .b(5'b01111), .out(subtractor_1_out));  // open: bin, bout
  Shifter #(.width(32)) shifter_1 (.in(bit_extender_1_out), .\dist (subtractor_1_out), .out(shifter_1_out));
  Shifter #(.width(32), .shift("ar")) shifter_2 (.in(shifter_1_out), .\dist (5'b01010), .out(shifter_2_out));
  Comparator #(.width(5)) comparator_1 (.a(subtractor_1_out), .b({5{1'b0}}), .lt(comparator_1_lt));  // open: gt, eq
  Multiplexer #(.width(32)) multiplexer_1 (
    .in0(shifter_2_out), .in1(subtractor_2_out), .out(multiplexer_1_out), .sel(sign));  // open: en
  Subtractor #(.width(32)) subtractor_2 (.a({32{1'b0}}), .b(shifter_2_out), .out(subtractor_2_out));  // open: bin, bout
  Multiplexer #(.width(32)) multiplexer_2 (
    .in0(multiplexer_1_out), .in1({32{1'b0}}), .out(out_4), .sel(comparator_1_lt));  // open: en
endmodule
