// Logisim project GRF.circ as structural Verilog: 1 circuit, main circuit grf
module grf (
  input  [31:0] WD,
  input  [4:0] RA1,
  input  [4:0] RA2,
  input  [4:0] WA,
  input  Clk,
  input  Reset,
  input  RegWrite,
  output [31:0] RD1,
  output [31:0] RD2
);

  wire [31:0] _0, _1, _2, _3, _4, _5, _6, _7, _8, _9, _10, _11, _12, _13, _14, _15, _16, _17, _18, _19, _20,
       _21, _22, _23, _24, _25, _26, _27, _28, _29, _30, _31, demultiplexer_1_out0, in1, in2, in3, in4, in5,
       in6, in7, in8, in9, in10, in11, in12, in13, in14, in15, in16, in17, in18, in19, in20, in21, in22,
       in23, in24, in25, in26, in27, in28, in29, in30, in31;

  Demultiplexer #(.select(5), .width(32), .tristate("true")) demultiplexer_1 (
    .out0(demultiplexer_1_out0), .out1(in1), .out2(in2), .out3(in3), .out4(in4), .out5(in5), .out6(in6),
    .out7(in7), .out8(in8), .out9(in9), .out10(in10), .out11(in11), .out12(in12), .out13(in13), .out14(in14),
    .out15(in15), .out16(in16), .out17(in17), .out18(in18), .out19(in19), .out20(in20), .out21(in21),
    .out22(in22), .out23(in23), .out24(in24), .out25(in25), .out26(in26), .out27(in27), .out28(in28),
    .out29(in29), .out30(in30), .out31(in31), .in(WD), .sel(WA));  // open: en
  Register #(.width(32)) register_1 (.D({32{1'b0}}), .en(RegWrite), .Q(_0), .clk(Clk), .clr(Reset));
  Register #(.width(32)) register_2 (.D(in4), .en(RegWrite), .Q(_4), .clk(Clk), .clr(Reset));
  Register #(.width(32)) register_3 (.D(in8), .en(RegWrite), .Q(_8), .clk(Clk), .clr(Reset));
  Register #(.width(32)) register_4 (.D(in12), .en(RegWrite), .Q(_12), .clk(Clk), .clr(Reset));
  Register #(.width(32)) register_5 (.D(in16), .en(RegWrite), .Q(_16), .clk(Clk), .clr(Reset));
  Register #(.width(32)) register_6 (.D(in20), .en(RegWrite), .Q(_20), .clk(Clk), .clr(Reset));
  Register #(.width(32)) register_7 (.D(in24), .en(RegWrite), .Q(_24), .clk(Clk), .clr(Reset));
  Register #(.width(32)) register_8 (.D(in28), .en(RegWrite), .Q(_28), .clk(Clk), .clr(Reset));
  Register #(.width(32)) register_9 (.D(in1), .en(RegWrite), .Q(_1), .clk(Clk), .clr(Reset));
  Register #(.width(32)) register_10 (.D(in5), .en(RegWrite), .Q(_5), .clk(Clk), .clr(Reset));
  Register #(.width(32)) register_11 (.D(in9), .en(RegWrite), .Q(_9), .clk(Clk), .clr(Reset));
  Register #(.width(32)) register_12 (.D(in13), .en(RegWrite), .Q(_13), .clk(Clk), .clr(Reset));
  Register #(.width(32)) register_13 (.D(in17), .en(RegWrite), .Q(_17), .clk(Clk), .clr(Reset));
  Register #(.width(32)) register_14 (.D(in21), .en(RegWrite), .Q(_21), .clk(Clk), .clr(Reset));
  Register #(.width(32)) register_15 (.D(in25), .en(RegWrite), .Q(_25), .clk(Clk), .clr(Reset));
  Register #(.width(32)) register_16 (.D(in29), .en(RegWrite), .Q(_29), .clk(Clk), .clr(Reset));
  Multiplexer #(.select(5), .width(32)) multiplexer_1 (
    .in0(_0), .in1(_1), .in2(_2), .in3(_3), .in4(_4), .in5(_5), .in6(_6), .in7(_7), .in8(_8), .in9(_9),
    .in10(_10), .in11(_11), .in12(_12), .in13(_13), .in14(_14), .in15(_15), .in16(_16), .in17(_17),
    .in18(_18), .in19(_19), .in20(_20), .in21(_21), .in22(_22), .in23(_23), .in24(_24), .in25(_25),
    .in26(_26), .in27(_27), .in28(_28), .in29(_29), .in30(_30), .in31(_31), .out(RD1), .sel(RA1));  // open: en
  Register #(.width(32)) register_17 (.D(in2), .en(RegWrite), .Q(_2), .clk(Clk), .clr(Reset));
  Register #(.width(32)) register_18 (.D(in6), .en(RegWrite), .Q(_6), .clk(Clk), .clr(Reset));
  Register #(.width(32)) register_19 (.D(in10), .en(RegWrite), .Q(_10), .clk(Clk), .clr(Reset));
  Register #(.width(32)) register_20 (.D(in14), .en(RegWrite), .Q(_14), .clk(Clk), .clr(Reset));
  Register #(.width(32)) register_21 (.D(in18), .en(RegWrite), .Q(_18), .clk(Clk), .clr(Reset));
  Register #(.width(32)) register_22 (.D(in22), .en(RegWrite), .Q(_22), .clk(Clk), .clr(Reset));
  Register #(.width(32)) register_23 (.D(in26), .en(RegWrite), .Q(_26), .clk(Clk), .clr(Reset));
  Register #(.width(32)) register_24 (.D(in30), .en(RegWrite), .Q(_30), .clk(Clk), .clr(Reset));
  Register #(.width(32)) register_25 (.D(in3), .en(RegWrite), .Q(_3), .clk(Clk), .clr(Reset));
  Register #(.width(32)) register_26 (.D(in7), .en(RegWrite), .Q(_7), .clk(Clk), .clr(Reset));
  Register #(.width(32)) register_27 (.D(in11), .en(RegWrite), .Q(_11), .clk(Clk), .clr(Reset));
  Register #(.width(32)) register_28 (.D(in15), .en(RegWrite), .Q(_15), .clk(Clk), .clr(Reset));
  Register #(.width(32)) register_29 (.D(in19), .en(RegWrite), .Q(_19), .clk(Clk), .clr(Reset));
  Register #(.width(32)) register_30 (.D(in23), .en(RegWrite), .Q(_23), .clk(Clk), .clr(Reset));
  Register #(.width(32)) register_31 (.D(in27), .en(RegWrite), .Q(_27), .clk(Clk), .clr(Reset));
  Register #(.width(32)) register_32 (.D(in31), .en(RegWrite), .Q(_31), .clk(Clk), .clr(Reset));
  Multiplexer #(.select(5), .width(32)) multiplexer_2 (
    .in0(_0), .in1(_1), .in2(_2), .in3(_3), .in4(_4), .in5(_5), .in6(_6), .in7(_7), .in8(_8), .in9(_9),
    .in10(_10), .in11(_11), .in12(_12), .in13(_13), .in14(_14), .in15(_15), .in16(_16), .in17(_17),
    .in18(_18), .in19(_19), .in20(_20), .in21(_21), .in22(_22), .in23(_23), .in24(_24), .in25(_25),
    .in26(_26), .in27(_27), .in28(_28), .in29(_29), .in30(_30), .in31(_31), .out(RD2), .sel(RA2));  // open: en

  // Other names for the same wires on the sheet: a1[4:0] = RA1; a2[4:0] = RA2; a3[4:0] = WA
endmodule
