// Logisim project Navigation.circ as structural Verilog: 3 circuits, main circuit navigation
module navigation (
  input  [1:0] dir,
  input  clk,
  input  reset,
  output arrive,
  output hit
);

  wire trans_1_hit;
  wire [2:0] register_1_q, trans_1_out_3;

  trans trans_1 (.in_1(register_1_q), .in_2(dir), .out_3(trans_1_out_3), .hit(trans_1_hit));
  Register #(.width(3)) register_1 (.D(trans_1_out_3), .Q(register_1_q), .clk(clk), .clr(reset));  // open: en
  Register #(.width(1)) register_2 (.D(trans_1_hit), .Q(hit), .clk(clk), .clr(reset));  // open: en
  \output  output_1 (.status(register_1_q), .arrive(arrive));
endmodule

module \output  (
  input  [2:0] status,
  output arrive
);

  wire not_1_out, not_2_out;

  not not_1 (not_1_out, status[0]);
  not not_2 (not_2_out, status[1]);
  and and_1 (arrive, not_1_out, not_2_out, status[2]);
endmodule

module trans (
  input  [2:0] in_1,
  input  [1:0] in_2,
  output [2:0] out_3,
  output hit
);

  wire and_1_out, and_2_out, and_3_out, and_4_out, and_5_out, and_6_out, and_7_out, and_8_out, and_9_out,
       and_10_out, and_11_out, and_12_out, and_13_out, and_14_out, and_15_out, and_16_out, not_1_out,
       not_2_out, not_3_out, not_4_out, not_5_out, not_6_out, not_7_out, not_8_out, not_9_out, not_10_out,
       not_11_out, not_12_out, not_13_out, not_14_out, not_15_out, not_16_out, not_17_out, not_18_out,
       not_19_out, not_20_out, not_21_out, not_22_out, not_23_out, not_24_out, not_25_out, not_26_out,
       not_27_out, not_28_out;

  not not_1 (not_1_out, in_1[0]);
  not not_2 (not_2_out, in_2[1]);
  not not_3 (not_3_out, in_2[0]);
  not not_4 (not_4_out, in_2[1]);
  not not_5 (not_5_out, in_1[0]);
  not not_6 (not_6_out, in_2[1]);
  not not_7 (not_7_out, in_1[0]);
  not not_8 (not_8_out, in_2[0]);
  not not_9 (not_9_out, in_1[2]);
  not not_10 (not_10_out, in_1[1]);
  not not_11 (not_11_out, in_2[1]);
  not not_12 (not_12_out, in_2[0]);
  not not_13 (not_13_out, in_1[2]);
  not not_14 (not_14_out, in_1[0]);
  not not_15 (not_15_out, in_2[1]);
  not not_16 (not_16_out, in_1[2]);
  not not_17 (not_17_out, in_1[1]);
  not not_18 (not_18_out, in_1[0]);
  not not_19 (not_19_out, in_1[2]);
  not not_20 (not_20_out, in_1[0]);
  not not_21 (not_21_out, in_2[0]);
  not not_22 (not_22_out, in_2[1]);
  not not_23 (not_23_out, in_2[0]);
  and and_1 (and_1_out, in_1[1], not_1_out, not_2_out, not_3_out);
  and and_2 (and_2_out, in_1[1], in_1[0], not_4_out, in_2[0]);
  not not_24 (not_24_out, in_1[1]);
  and and_3 (and_3_out, not_24_out, in_1[0], not_25_out);
  not not_25 (not_25_out, in_2[1]);
  and and_4 (and_4_out, in_1[0], not_26_out, not_27_out);
  not not_26 (not_26_out, in_2[1]);
  not not_27 (not_27_out, in_2[0]);
  and and_5 (and_5_out, in_1[1], not_5_out, not_6_out, in_2[0]);
  and and_6 (and_6_out, in_1[1], not_7_out, in_2[1], not_8_out);
  and and_7 (and_7_out, in_1[1], in_1[0], in_2[1], in_2[0]);
  and and_8 (and_8_out, not_9_out, not_10_out, not_11_out, not_12_out);
  and and_9 (and_9_out, in_1[0], in_2[1], in_2[0]);
  and and_10 (and_10_out, in_1[1], in_2[1], in_2[0]);
  and and_11 (and_11_out, in_1[1], in_1[0], not_28_out);
  not not_28 (not_28_out, in_2[0]);
  and and_12 (and_12_out, not_13_out, not_14_out, not_15_out, in_2[0]);
  and and_13 (and_13_out, not_16_out, not_17_out, not_18_out, in_2[1]);
  and and_14 (and_14_out, not_19_out, not_20_out, in_2[1], not_21_out);
  and and_15 (and_15_out, in_1[0], in_2[1], in_2[0]);
  and and_16 (and_16_out, in_1[1], in_1[0], not_22_out, not_23_out);
  or or_1 (out_3[2], and_1_out, and_2_out);
  or or_2 (out_3[1], and_3_out, and_4_out, and_5_out, and_6_out, and_7_out);
  or or_3 (out_3[0], and_8_out, and_9_out, and_10_out, and_11_out);
  or or_4 (hit, and_12_out, and_13_out, and_14_out, and_15_out, and_16_out);
endmodule
