// Logisim project Vote.circ as structural Verilog: 4 circuits, main circuit Vote
module Vote (
  input  [1:0] in_1,
  input  [1:0] in_2,
  input  [1:0] in_3,
  input  [1:0] in_4,
  output out_5
);

  wire comparator_1_eq, count_1_out_5;

  Comparator #(.width(2)) comparator_1 (.a(in_1), .b(2'b10), .eq(comparator_1_eq));  // open: gt, lt
  count count_1 (.in_1(in_1), .in_2(in_2), .in_3(in_3), .in_4(in_4), .out_5(count_1_out_5));
  Multiplexer multiplexer_1 (.in0(count_1_out_5), .in1(1'b0), .out(out_5), .sel(comparator_1_eq));  // open: en
endmodule

module count (
  input  [1:0] in_1,
  input  [1:0] in_2,
  input  [1:0] in_3,
  input  [1:0] in_4,
  output out_5
);

  wire trans_1_agree, trans_1_disagree, trans_2_agree, trans_2_disagree, trans_3_agree, trans_3_disagree,
       trans_4_agree, trans_4_disagree;
  wire [2:0] add_4_1_out_5, add_4_2_out_5;

  trans trans_1 (.in_1(in_1), .agree(trans_1_agree), .disagree(trans_1_disagree));
  trans trans_2 (.in_1(in_2), .agree(trans_2_agree), .disagree(trans_2_disagree));
  trans trans_3 (.in_1(in_3), .agree(trans_3_agree), .disagree(trans_3_disagree));
  trans trans_4 (.in_1(in_4), .agree(trans_4_agree), .disagree(trans_4_disagree));
  add_4 add_4_1 (
    .in_1(trans_1_agree), .in_2(trans_2_agree), .in_3(trans_3_agree), .in_4(trans_4_agree),
    .out_5(add_4_1_out_5));
  add_4 add_4_2 (
    .in_1(trans_1_disagree), .in_2(trans_2_disagree), .in_3(trans_3_disagree), .in_4(trans_4_disagree),
    .out_5(add_4_2_out_5));
  Comparator #(.width(3)) comparator_1 (.a(add_4_1_out_5), .b(add_4_2_out_5), .gt(out_5));  // open: eq, lt
endmodule

module trans (
  input  [1:0] in_1,
  output agree,
  output disagree
);

  Comparator #(.width(2)) comparator_1 (.a(in_1), .b(2'b11), .eq(agree));  // open: gt, lt
  Comparator #(.width(2)) comparator_2 (.a(in_1), .b(2'b00), .eq(disagree));  // open: gt, lt
endmodule

module add_4 (
  input  in_1,
  input  in_2,
  input  in_3,
  input  in_4,
  output [2:0] out_5
);

  wire [2:0] adder_1_out, adder_2_out, bit_extender_1_out, bit_extender_2_out, bit_extender_3_out,
       bit_extender_4_out;

  assign bit_extender_1_out = {{2{1'b0}}, in_1};  // Bit_Extender bit_extender_1
  assign bit_extender_2_out = {{2{1'b0}}, in_2};  // Bit_Extender bit_extender_2
  assign bit_extender_3_out = {{2{1'b0}}, in_3};  // Bit_Extender bit_extender_3
  assign bit_extender_4_out = {{2{1'b0}}, in_4};  // Bit_Extender bit_extender_4
  Adder #(.width(3)) adder_1 (.a(bit_extender_1_out), .b(bit_extender_2_out), .out(adder_1_out));  // open: cin, cout
  Adder #(.width(3)) adder_2 (.a(bit_extender_3_out), .b(bit_extender_4_out), .out(adder_2_out));  // open: cin, cout
  Adder #(.width(3)) adder_3 (.a(adder_1_out), .b(adder_2_out), .out(out_5));  // open: cin, cout
endmodule
