// Logisim project P3(orig).circ as structural Verilog: 10 circuits, main circuit main
module main (
  input  Reset,
  output [31:0] out_2,
  output out_3,
  output [4:0] out_4,
  output [31:0] out_5,
  output out_6,
  output [4:0] out_7,
  output [31:0] out_8
);

  wire ALUSrc, Branch1, Branch2, Branch3, Clk, EXTOp, MemRead, Zero;
  wire [1:0] MemToReg, RegDst;
  wire [2:0] ALUCtr, ALUOp;
  wire [31:0] ALUResult, dm_1_rd, Imm32, multiplexer_2_out, multiplexer_3_out, multiplexer_4_out, PC_4, RD1,
       shift_1_output;

  Clock u_Clk (.out(Clk));
  IFU ifu_1 (
    .Clk(Clk), .Reset(Reset), .Zero(Zero), .Branch1(Branch1), .Imm32(Imm32), .Instr(out_2),
    .Branch2(Branch2), .Branch3(Branch3), .PC_4(PC_4), .Result({ALUResult[31:7], out_7, ALUResult[1:0]}));
  Controller controller_1 (
    .Op(out_2[31:26]), .RegDst(RegDst), .ALUSrc(ALUSrc), .RegWrite(out_3), .MemRead(MemRead),
    .MemWrite(out_6), .MemToReg(MemToReg), .EXTOp(EXTOp), .Branch1(Branch1), .Branch2(Branch2), .ALUOp(ALUOp));
  ALUController alucontroller_1 (.ALUOp(ALUOp), .Func(out_2[5:0]), .ALUCtr(ALUCtr), .Branch3(Branch3));
  Multiplexer #(.select(2), .width(5)) multiplexer_1 (
    .in0(out_2[20:16]), .in1(out_2[15:11]), .in2({5{1'b1}}), .in3({5{1'b0}}), .out(out_4), .sel(RegDst));  // open: en
  Multiplexer #(.width(32)) multiplexer_2 (
    .in0(out_8), .in1(Imm32), .out(multiplexer_2_out), .sel(ALUSrc));  // open: en
  Shift shift_1 (.Input(Imm32), .Distance(5'b10000), .Output(shift_1_output));
  ALU alu_1 (
    .A(RD1), .B(multiplexer_2_out), .ALUCtrl(ALUCtr), .Result({ALUResult[31:7], out_7, ALUResult[1:0]}),
    .Zero(Zero));
  DM dm_1 (.Clk(Clk), .Reset(Reset), .MemWrite(out_6), .MemRead(MemRead), .A(out_7), .WD(out_8), .RD(dm_1_rd));
  Multiplexer #(.width(32)) multiplexer_3 (
    .in0(shift_1_output), .in1(PC_4), .out(multiplexer_3_out), .sel(Branch2));  // open: en
  GRF grf_1 (
    .WD(out_5), .RA1(out_2[25:21]), .RA2(out_2[20:16]), .WA(out_4), .Clk(Clk), .Reset(Reset),
    .RegWrite(out_3), .RD1(RD1), .RD2(out_8));
  EXT ext_1 (.In(out_2[15:0]), .ExtOp(EXTOp), .Out(Imm32));
  Multiplexer #(.width(32)) multiplexer_4 (
    .in0({ALUResult[31:7], out_7, ALUResult[1:0]}), .in1(dm_1_rd), .out(multiplexer_4_out), .sel(MemToReg[1]));  // open: en
  Multiplexer #(.width(32)) multiplexer_5 (
    .in0(multiplexer_4_out), .in1(multiplexer_3_out), .out(out_5), .sel(MemToReg[0]));  // open: en

  // Other names for the same wires on the sheet: ALUResult[6:2] = out_7; MemAddr[4:0] = out_7; Func[5:0] = out_2[5:0];
  //   Imm16[15:0] = out_2[15:0]; Instr[31:0] = out_2; Instr_15_11[4:0] = out_2[15:11];
  //   Instr_20_16[4:0] = out_2[20:16]; Instr_25_21[4:0] = out_2[25:21]; MemWrite = out_6; OPCode[5:0] = out_2[31:26];
  //   RD2[31:0] = out_8; RegAddr[4:0] = out_4; RegWrite = out_3; WD[31:0] = out_5
endmodule

module IM (
  input  [4:0] A,
  output [31:0] out_2
);

  ROM #(.addrWidth(5), .dataWidth(32)) rom_1 (.addr(A), .data(out_2));  // open: sel

  // Notes on the sheet:
  //   contents of rom_1 (hex, n*v repeats v):
  //   340407cf 3485006f 3c063039 3c07ffff 34e7ffff 858021 e78821 f09021 928023 e78823 e49023 2519823
  //   34080000 ad040000 0 ad050004 ad100008 ad11000c ad120010 8d0f0000 8d0e0014 ad0e0018 8d0d000c 35080001
  //   35290001 354a0002 110affef 11090001 3c0b0457 10f4021
endmodule

module IFU (
  input  Clk,
  input  Reset,
  input  Zero,
  input  Branch1,
  input  Branch2,
  input  Branch3,
  input  [31:0] Imm32,
  input  [31:0] Result,
  output [31:0] Instr,
  output [31:0] PC_4
);

  wire and_1_out;
  wire [4:0] PC_q_2;
  wire [27:0] PC_q;
  wire [31:0] adder_2_out, multiplexer_1_out, multiplexer_2_out, multiplexer_3_out, shift_1_output;
  wire [31:28] PCj;

  IM im_1 (.A(PC_q_2), .out_2(Instr));
  Register #(.width(32)) PC (
    .D(multiplexer_3_out), .Q({PCj, PC_q[27:7], PC_q_2, PC_q[1:0]}), .clk(Clk), .clr(Reset));  // open: en
  Adder #(.width(32)) adder_1 (.a(32'h4), .b({PCj, PC_q[27:7], PC_q_2, PC_q[1:0]}), .out(PC_4));  // open: cin, cout
  Shift shift_1 (.Input(Imm32), .Distance(5'b00010), .Output(shift_1_output));
  Adder #(.width(32)) adder_2 (.a(PC_4), .b(shift_1_output), .out(adder_2_out));  // open: cin, cout
  Multiplexer #(.width(32)) multiplexer_1 (
    .in0(PC_4), .in1(adder_2_out), .out(multiplexer_1_out), .sel(and_1_out));  // open: en
  and and_1 (and_1_out, Zero, Branch1);
  Multiplexer #(.width(32)) multiplexer_2 (
    .in0(multiplexer_1_out), .in1({PCj, Instr[25:0], 2'b00}), .out(multiplexer_2_out), .sel(Branch2));  // open: en
  Multiplexer #(.width(32)) multiplexer_3 (
    .in0(multiplexer_2_out), .in1(Result), .out(multiplexer_3_out), .sel(Branch3));  // open: en

  // Other names for the same wires on the sheet: PCj[27:2] = Instr[25:0]
endmodule

module Shift (
  input  [31:0] Input,
  input  [4:0] Distance,
  output [31:0] Output
);

  Shifter #(.width(32)) shifter_1 (.in(Input), .\dist (Distance), .out(Output));
endmodule

module GRF (
  input  [31:0] WD,
  input  [4:0] RA1,
  input  [4:0] RA2,
  input  [4:0] WA,
  input  Clk,
  input  Reset,
  input  RegWrite,
  output [31:0] RD1,
  output [31:0] RD2
);

  wire [31:0] _0, _1, _2, _3, _4, _5, _6, _7, _8, _9, _10, _11, _12, _13, _14, _15, _16, _17, _18, _19, _20,
       _21, _22, _23, _24, _25, _26, _27, _28, _29, _30, _31, demultiplexer_1_out0, in1, in2, in3, in4, in5,
       in6, in7, in8, in9, in10, in11, in12, in13, in14, in15, in16, in17, in18, in19, in20, in21, in22,
       in23, in24, in25, in26, in27, in28, in29, in30, in31;

  Demultiplexer #(.select(5), .width(32), .tristate("true")) demultiplexer_1 (
    .out0(demultiplexer_1_out0), .out1(in1), .out2(in2), .out3(in3), .out4(in4), .out5(in5), .out6(in6),
    .out7(in7), .out8(in8), .out9(in9), .out10(in10), .out11(in11), .out12(in12), .out13(in13), .out14(in14),
    .out15(in15), .out16(in16), .out17(in17), .out18(in18), .out19(in19), .out20(in20), .out21(in21),
    .out22(in22), .out23(in23), .out24(in24), .out25(in25), .out26(in26), .out27(in27), .out28(in28),
    .out29(in29), .out30(in30), .out31(in31), .in(WD), .sel(WA));  // open: en
  Register #(.width(32)) register_1 (.D({32{1'b0}}), .en(RegWrite), .Q(_0), .clk(Clk), .clr(Reset));
  Register #(.width(32)) register_2 (.D(in4), .en(RegWrite), .Q(_4), .clk(Clk), .clr(Reset));
  Register #(.width(32)) register_3 (.D(in8), .en(RegWrite), .Q(_8), .clk(Clk), .clr(Reset));
  Register #(.width(32)) register_4 (.D(in12), .en(RegWrite), .Q(_12), .clk(Clk), .clr(Reset));
  Register #(.width(32)) register_5 (.D(in16), .en(RegWrite), .Q(_16), .clk(Clk), .clr(Reset));
  Register #(.width(32)) register_6 (.D(in20), .en(RegWrite), .Q(_20), .clk(Clk), .clr(Reset));
  Register #(.width(32)) register_7 (.D(in24), .en(RegWrite), .Q(_24), .clk(Clk), .clr(Reset));
  Register #(.width(32)) register_8 (.D(in28), .en(RegWrite), .Q(_28), .clk(Clk), .clr(Reset));
  Register #(.width(32)) register_9 (.D(in1), .en(RegWrite), .Q(_1), .clk(Clk), .clr(Reset));
  Register #(.width(32)) register_10 (.D(in5), .en(RegWrite), .Q(_5), .clk(Clk), .clr(Reset));
  Register #(.width(32)) register_11 (.D(in9), .en(RegWrite), .Q(_9), .clk(Clk), .clr(Reset));
  Register #(.width(32)) register_12 (.D(in13), .en(RegWrite), .Q(_13), .clk(Clk), .clr(Reset));
  Register #(.width(32)) register_13 (.D(in17), .en(RegWrite), .Q(_17), .clk(Clk), .clr(Reset));
  Register #(.width(32)) register_14 (.D(in21), .en(RegWrite), .Q(_21), .clk(Clk), .clr(Reset));
  Register #(.width(32)) register_15 (.D(in25), .en(RegWrite), .Q(_25), .clk(Clk), .clr(Reset));
  Register #(.width(32)) register_16 (.D(in29), .en(RegWrite), .Q(_29), .clk(Clk), .clr(Reset));
  Multiplexer #(.select(5), .width(32)) multiplexer_1 (
    .in0(_0), .in1(_1), .in2(_2), .in3(_3), .in4(_4), .in5(_5), .in6(_6), .in7(_7), .in8(_8), .in9(_9),
    .in10(_10), .in11(_11), .in12(_12), .in13(_13), .in14(_14), .in15(_15), .in16(_16), .in17(_17),
    .in18(_18), .in19(_19), .in20(_20), .in21(_21), .in22(_22), .in23(_23), .in24(_24), .in25(_25),
    .in26(_26), .in27(_27), .in28(_28), .in29(_29), .in30(_30), .in31(_31), .out(RD1), .sel(RA1));  // open: en
  Register #(.width(32)) register_17 (.D(in2), .en(RegWrite), .Q(_2), .clk(Clk), .clr(Reset));
  Register #(.width(32)) register_18 (.D(in6), .en(RegWrite), .Q(_6), .clk(Clk), .clr(Reset));
  Register #(.width(32)) register_19 (.D(in10), .en(RegWrite), .Q(_10), .clk(Clk), .clr(Reset));
  Register #(.width(32)) register_20 (.D(in14), .en(RegWrite), .Q(_14), .clk(Clk), .clr(Reset));
  Register #(.width(32)) register_21 (.D(in18), .en(RegWrite), .Q(_18), .clk(Clk), .clr(Reset));
  Register #(.width(32)) register_22 (.D(in22), .en(RegWrite), .Q(_22), .clk(Clk), .clr(Reset));
  Register #(.width(32)) register_23 (.D(in26), .en(RegWrite), .Q(_26), .clk(Clk), .clr(Reset));
  Register #(.width(32)) register_24 (.D(in30), .en(RegWrite), .Q(_30), .clk(Clk), .clr(Reset));
  Register #(.width(32)) register_25 (.D(in3), .en(RegWrite), .Q(_3), .clk(Clk), .clr(Reset));
  Register #(.width(32)) register_26 (.D(in7), .en(RegWrite), .Q(_7), .clk(Clk), .clr(Reset));
  Register #(.width(32)) register_27 (.D(in11), .en(RegWrite), .Q(_11), .clk(Clk), .clr(Reset));
  Register #(.width(32)) register_28 (.D(in15), .en(RegWrite), .Q(_15), .clk(Clk), .clr(Reset));
  Register #(.width(32)) register_29 (.D(in19), .en(RegWrite), .Q(_19), .clk(Clk), .clr(Reset));
  Register #(.width(32)) register_30 (.D(in23), .en(RegWrite), .Q(_23), .clk(Clk), .clr(Reset));
  Register #(.width(32)) register_31 (.D(in27), .en(RegWrite), .Q(_27), .clk(Clk), .clr(Reset));
  Register #(.width(32)) register_32 (.D(in31), .en(RegWrite), .Q(_31), .clk(Clk), .clr(Reset));
  Multiplexer #(.select(5), .width(32)) multiplexer_2 (
    .in0(_0), .in1(_1), .in2(_2), .in3(_3), .in4(_4), .in5(_5), .in6(_6), .in7(_7), .in8(_8), .in9(_9),
    .in10(_10), .in11(_11), .in12(_12), .in13(_13), .in14(_14), .in15(_15), .in16(_16), .in17(_17),
    .in18(_18), .in19(_19), .in20(_20), .in21(_21), .in22(_22), .in23(_23), .in24(_24), .in25(_25),
    .in26(_26), .in27(_27), .in28(_28), .in29(_29), .in30(_30), .in31(_31), .out(RD2), .sel(RA2));  // open: en

  // Other names for the same wires on the sheet: a1[4:0] = RA1; a2[4:0] = RA2; a3[4:0] = WA
endmodule

module ALU (
  input  [31:0] A,
  input  [31:0] B,
  input  [2:0] ALUCtrl,
  output [31:0] Result,
  output Zero
);

  wire or_2_out;
  wire [0:0] Compare;
  wire [31:0] Add, And, Or, Sub;

  assign And = A & B;  // AND_Gate and_1, 32 bits wide
  assign Or = A | B;  // OR_Gate or_1, 32 bits wide
  Adder #(.width(32)) adder_1 (.a(A), .b(B), .out(Add));  // open: cin, cout
  Subtractor #(.width(32)) subtractor_1 (.a(A), .b(B), .out(Sub));  // open: bin, bout
  Comparator #(.width(32)) comparator_1 (.a(A), .b(B), .gt(Compare[0]));  // open: eq, lt
  Multiplexer #(.select(3), .width(32)) multiplexer_1 (
    .in0(And), .in1(Or), .in2(Add), .in3(Sub), .in5({{31{1'b0}}, Compare[0]}), .out(Result), .sel(ALUCtrl));  // open: in4, in6, in7, en
  or or_2 (or_2_out, Sub[0], Sub[1], Sub[2], Sub[3], Sub[4], Sub[5], Sub[6], Sub[7], Sub[8], Sub[9], Sub[10], Sub[11], Sub[12], Sub[13], Sub[14], Sub[15], Sub[17], Sub[18], Sub[19], Sub[20], Sub[21], Sub[22], Sub[23], Sub[24], Sub[25], Sub[26], Sub[27], Sub[28], Sub[29], Sub[30], Sub[31], Sub[16]);
  not not_1 (Zero, or_2_out);

  // Other names for the same wires on the sheet: ctrl[2:0] = ALUCtrl
endmodule

module DM (
  input  Clk,
  input  Reset,
  input  MemWrite,
  input  MemRead,
  input  [4:0] A,
  input  [31:0] WD,
  output [31:0] RD
);

  RAM #(.addrWidth(5), .dataWidth(32), .bus("separate")) ram_1 (
    .addr(A), .din(WD), .data(RD), .str(MemWrite), .clk(Clk), .ld(MemRead), .clr(Reset));  // open: sel

  // Other names for the same wires on the sheet: addr[4:0] = A; mr = MemRead; mw = MemWrite
endmodule

module EXT (
  input  [15:0] In,
  input  ExtOp,
  output [31:0] Out
);

  wire [31:0] bit_extender_1_out, bit_extender_2_out;

  assign bit_extender_1_out = {{16{In[15]}}, In};  // Bit_Extender bit_extender_1
  assign bit_extender_2_out = {{16{1'b0}}, In};  // Bit_Extender bit_extender_2
  Multiplexer #(.width(32)) multiplexer_1 (
    .in0(bit_extender_1_out), .in1(bit_extender_2_out), .out(Out), .sel(ExtOp));  // open: en
endmodule

module Controller (
  input  [5:0] Op,
  output [1:0] RegDst,
  output ALUSrc,
  output RegWrite,
  output MemRead,
  output MemWrite,
  output [1:0] MemToReg,
  output EXTOp,
  output Branch1,
  output Branch2,
  output [2:0] ALUOp
);

  wire lui_out, not_1_out, not_2_out, not_3_out, not_4_out, not_5_out, not_6_out;

  not not_1 (not_1_out, Op[5]);
  not not_2 (not_2_out, Op[4]);
  not not_3 (not_3_out, Op[3]);
  not not_4 (not_4_out, Op[2]);
  not not_5 (not_5_out, Op[0]);
  not not_6 (not_6_out, Op[1]);
  and R (RegDst[0], not_1_out, not_2_out, not_3_out, not_4_out, not_6_out, not_5_out);
  and lw (MemRead, Op[5], not_2_out, not_3_out, not_4_out, Op[1], Op[0]);
  and sw (MemWrite, Op[5], not_2_out, Op[3], not_4_out, Op[1], Op[0]);
  and beq (Branch1, not_1_out, not_2_out, not_3_out, Op[2], not_6_out, not_5_out);
  and lui (lui_out, not_1_out, not_2_out, Op[3], Op[2], Op[1], Op[0]);
  and ori (ALUOp[2], not_1_out, not_2_out, Op[3], Op[2], not_6_out, Op[0]);
  and j (Branch2, not_1_out, not_2_out, not_3_out, not_4_out, Op[1], not_5_out);
  and jal (RegDst[1], not_1_out, not_2_out, not_3_out, not_4_out, Op[1], Op[0]);
  or or_1 (ALUSrc, MemRead, MemWrite, ALUOp[2]);
  or or_2 (RegWrite, RegDst[0], MemRead, RegDst[1], lui_out, ALUOp[2]);
  or or_3 (MemToReg[1], RegDst[1], MemRead);
  or or_4 (MemToReg[0], lui_out, RegDst[1]);
  or or_5 (ALUOp[1], Branch1, lui_out, RegDst[1], ALUOp[2], Branch2);
  or or_6 (ALUOp[0], lui_out, MemRead, MemWrite, ALUOp[2], Branch2, RegDst[1]);

  assign EXTOp = ALUOp[2];
endmodule

module ALUController (
  input  [2:0] ALUOp,
  input  [5:0] Func,
  output [2:0] ALUCtr,
  output Branch3
);

  wire addu_out, beq_out, not_1_out, not_2_out, not_3_out, not_4_out, not_5_out, not_6_out, not_7_out,
       not_8_out, not_9_out, ori_out, subu_out, sw_lw_out;

  not not_1 (not_1_out, ALUOp[2]);
  not not_2 (not_2_out, ALUOp[1]);
  not not_3 (not_3_out, ALUOp[0]);
  not not_4 (not_4_out, Func[5]);
  not not_5 (not_5_out, Func[4]);
  not not_6 (not_6_out, Func[3]);
  not not_7 (not_7_out, Func[2]);
  not not_8 (not_8_out, Func[0]);
  not not_9 (not_9_out, Func[1]);
  and sw_lw (sw_lw_out, not_1_out, not_2_out, ALUOp[0]);
  and beq (beq_out, not_1_out, ALUOp[1], not_3_out);
  and lui_j_jal (ALUCtr[2], not_1_out, ALUOp[1], ALUOp[0]);
  and ori (ori_out, ALUOp[2], ALUOp[1], ALUOp[0]);
  and addu (addu_out, not_1_out, not_2_out, not_3_out, Func[5], not_5_out, not_6_out, not_7_out, not_9_out, Func[0]);
  and subu (subu_out, not_1_out, not_2_out, not_3_out, Func[5], not_5_out, not_6_out, not_7_out, Func[1], Func[0]);
  and jr (Branch3, not_1_out, not_2_out, not_3_out, not_4_out, not_5_out, Func[3], not_7_out, not_9_out, not_8_out);
  or or_1 (ALUCtr[1], ALUCtr[2], sw_lw_out, beq_out, addu_out, subu_out, Branch3);
  or or_2 (ALUCtr[0], beq_out, ALUCtr[2], Branch3, ori_out, subu_out);
endmodule
