// Logisim project Single_Cycle_CPU.circ as structural Verilog: 11 circuits, main circuit main
module main (
  input  Reset,
  output [31:0] out_2,
  output out_3,
  output [4:0] out_4,
  output [31:0] out_5,
  output out_6,
  output [4:0] out_7,
  output [31:0] out_8
);

  wire alu_1_zero, ALUSrc, clk, ctrl_1_branch, ExtOp, Jump, PCSrc;
  wire [1:0] MemToReg, RegDst;
  wire [2:0] ALUCtrl, ctrl_1_aluop;
  wire [4:0] splitter_1__15_11, splitter_1__20_16, splitter_1__25_21;
  wire [5:0] splitter_1_func, splitter_1_opcode;
  wire [15:0] splitter_1_imm16;
  wire [27:0] ifu_1_pc;
  wire [31:0] adder_1_out, adder_2_out, alu_1_result, dm_1_rd, ext_1_out, grf_1_rd1, leftshift2_1_out_2,
       leftshift16_1_out_2, multiplexer_1_out, multiplexer_2_out, multiplexer_4_out;
  wire [31:2] splitter_1__25_0;

  Multiplexer #(.width(32)) multiplexer_1 (
    .in0(adder_1_out), .in1(adder_2_out), .out(multiplexer_1_out), .sel(PCSrc));  // open: en
  Multiplexer #(.width(32)) multiplexer_2 (
    .in0(multiplexer_1_out), .in1({splitter_1__25_0, 2'b00}), .out(multiplexer_2_out), .sel(Jump));  // open: en
  IFU ifu_1 (
    .Clk(clk), .Reset(Reset), .next_PC(multiplexer_2_out), .Instr(out_2),
    .PC({splitter_1__25_0[31:28], ifu_1_pc}));
  Splitter splitter_1 (
    .Instr(out_2), .Func(splitter_1_func), .Imm16(splitter_1_imm16), ._15_11(splitter_1__15_11),
    ._20_16(splitter_1__20_16), ._25_21(splitter_1__25_21), .OPCode(splitter_1_opcode),
    ._25_0(splitter_1__25_0[27:2]));
  Adder #(.width(32)) adder_1 (
    .a(32'h4), .b({splitter_1__25_0[31:28], ifu_1_pc}), .out(adder_1_out));  // open: cin, cout
  Clock u_Clk (.out(clk));
  Ctrl ctrl_1 (
    .Op(splitter_1_opcode), .RegDst(RegDst), .ALUSrc(ALUSrc), .RegWrite(out_3), .MemWrite(out_6),
    .MemToReg(MemToReg), .EXTOp(ExtOp), .Branch(ctrl_1_branch), .Jump(Jump), .ALUOp(ctrl_1_aluop));
  ALUCtrl aluctrl_1 (.ALUOp(ctrl_1_aluop), .Func(splitter_1_func), .ALUCtr(ALUCtrl));
  Multiplexer #(.select(2), .width(5)) multiplexer_3 (
    .in0(splitter_1__20_16), .in1(splitter_1__15_11), .in2({5{1'b1}}), .in3({5{1'b0}}), .out(out_4),
    .sel(RegDst));  // open: en
  GRF grf_1 (
    .WD(out_5), .A1(splitter_1__25_21), .A2(splitter_1__20_16), .A3(out_4), .Clk(clk), .Reset(Reset),
    .RegWrite(out_3), .RD1(grf_1_rd1), .RD2(out_8));
  EXT ext_1 (.In(splitter_1_imm16), .ExtOp(ExtOp), .Out(ext_1_out));
  Multiplexer #(.width(32)) multiplexer_4 (
    .in0(out_8), .in1(ext_1_out), .out(multiplexer_4_out), .sel(ALUSrc));  // open: en
  LeftShift16 leftshift16_1 (.in_1(ext_1_out), .out_2(leftshift16_1_out_2));
  LeftShift2 leftshift2_1 (.in_1(ext_1_out), .out_2(leftshift2_1_out_2));
  ALU alu_1 (
    .A(grf_1_rd1), .B(multiplexer_4_out), .ALUCtrl(ALUCtrl),
    .Result({alu_1_result[31:7], out_7, alu_1_result[1:0]}), .Zero(alu_1_zero));
  Adder #(.width(32)) adder_2 (.a(leftshift2_1_out_2), .b(adder_1_out), .out(adder_2_out));  // open: cin, cout
  and and_1 (PCSrc, ctrl_1_branch, alu_1_zero);
  DM dm_1 (.Clk(clk), .Reset(Reset), .MemWrite(out_6), .A(out_7), .WD(out_8), .RD(dm_1_rd));
  Multiplexer #(.select(2), .width(32)) multiplexer_5 (
    .in0({alu_1_result[31:7], out_7, alu_1_result[1:0]}), .in1(dm_1_rd), .in2(leftshift16_1_out_2),
    .out(out_5), .sel(MemToReg));  // open: in3, en

  // Other names for the same wires on the sheet: MemAddr[4:0] = out_7; Instr[31:0] = out_2; MemData[31:0] = out_8;
  //   MemWrite = out_6; RegAddr[4:0] = out_4; RegData[31:0] = out_5; RegWrite = out_3
endmodule

module GRF (
  input  [31:0] WD,
  input  [4:0] A1,
  input  [4:0] A2,
  input  [4:0] A3,
  input  Clk,
  input  Reset,
  input  RegWrite,
  output [31:0] RD1,
  output [31:0] RD2
);

  wire [31:0] _0, _1, _2, _3, _4, _5, _6, _7, _8, _9, _10, _11, _12, _13, _14, _15, _16, _17, _18, _19, _20,
       _21, _22, _23, _24, _25, _26, _27, _28, _29, _30, _31, demultiplexer_1_out0, in1, in2, in3, in4, in5,
       in6, in7, in8, in9, in10, in11, in12, in13, in14, in15, in16, in17, in18, in19, in20, in21, in22,
       in23, in24, in25, in26, in27, in28, in29, in30, in31;

  Demultiplexer #(.select(5), .width(32), .tristate("true")) demultiplexer_1 (
    .out0(demultiplexer_1_out0), .out1(in1), .out2(in2), .out3(in3), .out4(in4), .out5(in5), .out6(in6),
    .out7(in7), .out8(in8), .out9(in9), .out10(in10), .out11(in11), .out12(in12), .out13(in13), .out14(in14),
    .out15(in15), .out16(in16), .out17(in17), .out18(in18), .out19(in19), .out20(in20), .out21(in21),
    .out22(in22), .out23(in23), .out24(in24), .out25(in25), .out26(in26), .out27(in27), .out28(in28),
    .out29(in29), .out30(in30), .out31(in31), .in(WD), .sel(A3));  // open: en
  Register #(.width(32)) register_1 (.D({32{1'b0}}), .en(RegWrite), .Q(_0), .clk(Clk), .clr(Reset));
  Register #(.width(32)) register_2 (.D(in4), .en(RegWrite), .Q(_4), .clk(Clk), .clr(Reset));
  Register #(.width(32)) register_3 (.D(in8), .en(RegWrite), .Q(_8), .clk(Clk), .clr(Reset));
  Register #(.width(32)) register_4 (.D(in12), .en(RegWrite), .Q(_12), .clk(Clk), .clr(Reset));
  Register #(.width(32)) register_5 (.D(in16), .en(RegWrite), .Q(_16), .clk(Clk), .clr(Reset));
  Register #(.width(32)) register_6 (.D(in20), .en(RegWrite), .Q(_20), .clk(Clk), .clr(Reset));
  Register #(.width(32)) register_7 (.D(in24), .en(RegWrite), .Q(_24), .clk(Clk), .clr(Reset));
  Register #(.width(32)) register_8 (.D(in28), .en(RegWrite), .Q(_28), .clk(Clk), .clr(Reset));
  Register #(.width(32)) register_9 (.D(in1), .en(RegWrite), .Q(_1), .clk(Clk), .clr(Reset));
  Register #(.width(32)) register_10 (.D(in5), .en(RegWrite), .Q(_5), .clk(Clk), .clr(Reset));
  Register #(.width(32)) register_11 (.D(in9), .en(RegWrite), .Q(_9), .clk(Clk), .clr(Reset));
  Register #(.width(32)) register_12 (.D(in13), .en(RegWrite), .Q(_13), .clk(Clk), .clr(Reset));
  Register #(.width(32)) register_13 (.D(in17), .en(RegWrite), .Q(_17), .clk(Clk), .clr(Reset));
  Register #(.width(32)) register_14 (.D(in21), .en(RegWrite), .Q(_21), .clk(Clk), .clr(Reset));
  Register #(.width(32)) register_15 (.D(in25), .en(RegWrite), .Q(_25), .clk(Clk), .clr(Reset));
  Register #(.width(32)) register_16 (.D(in29), .en(RegWrite), .Q(_29), .clk(Clk), .clr(Reset));
  Multiplexer #(.select(5), .width(32)) multiplexer_1 (
    .in0(_0), .in1(_1), .in2(_2), .in3(_3), .in4(_4), .in5(_5), .in6(_6), .in7(_7), .in8(_8), .in9(_9),
    .in10(_10), .in11(_11), .in12(_12), .in13(_13), .in14(_14), .in15(_15), .in16(_16), .in17(_17),
    .in18(_18), .in19(_19), .in20(_20), .in21(_21), .in22(_22), .in23(_23), .in24(_24), .in25(_25),
    .in26(_26), .in27(_27), .in28(_28), .in29(_29), .in30(_30), .in31(_31), .out(RD1), .sel(A1));  // open: en
  Register #(.width(32)) register_17 (.D(in2), .en(RegWrite), .Q(_2), .clk(Clk), .clr(Reset));
  Register #(.width(32)) register_18 (.D(in6), .en(RegWrite), .Q(_6), .clk(Clk), .clr(Reset));
  Register #(.width(32)) register_19 (.D(in10), .en(RegWrite), .Q(_10), .clk(Clk), .clr(Reset));
  Register #(.width(32)) register_20 (.D(in14), .en(RegWrite), .Q(_14), .clk(Clk), .clr(Reset));
  Register #(.width(32)) register_21 (.D(in18), .en(RegWrite), .Q(_18), .clk(Clk), .clr(Reset));
  Register #(.width(32)) register_22 (.D(in22), .en(RegWrite), .Q(_22), .clk(Clk), .clr(Reset));
  Register #(.width(32)) register_23 (.D(in26), .en(RegWrite), .Q(_26), .clk(Clk), .clr(Reset));
  Register #(.width(32)) register_24 (.D(in30), .en(RegWrite), .Q(_30), .clk(Clk), .clr(Reset));
  Register #(.width(32)) register_25 (.D(in3), .en(RegWrite), .Q(_3), .clk(Clk), .clr(Reset));
  Register #(.width(32)) register_26 (.D(in7), .en(RegWrite), .Q(_7), .clk(Clk), .clr(Reset));
  Register #(.width(32)) register_27 (.D(in11), .en(RegWrite), .Q(_11), .clk(Clk), .clr(Reset));
  Register #(.width(32)) register_28 (.D(in15), .en(RegWrite), .Q(_15), .clk(Clk), .clr(Reset));
  Register #(.width(32)) register_29 (.D(in19), .en(RegWrite), .Q(_19), .clk(Clk), .clr(Reset));
  Register #(.width(32)) register_30 (.D(in23), .en(RegWrite), .Q(_23), .clk(Clk), .clr(Reset));
  Register #(.width(32)) register_31 (.D(in27), .en(RegWrite), .Q(_27), .clk(Clk), .clr(Reset));
  Register #(.width(32)) register_32 (.D(in31), .en(RegWrite), .Q(_31), .clk(Clk), .clr(Reset));
  Multiplexer #(.select(5), .width(32)) multiplexer_2 (
    .in0(_0), .in1(_1), .in2(_2), .in3(_3), .in4(_4), .in5(_5), .in6(_6), .in7(_7), .in8(_8), .in9(_9),
    .in10(_10), .in11(_11), .in12(_12), .in13(_13), .in14(_14), .in15(_15), .in16(_16), .in17(_17),
    .in18(_18), .in19(_19), .in20(_20), .in21(_21), .in22(_22), .in23(_23), .in24(_24), .in25(_25),
    .in26(_26), .in27(_27), .in28(_28), .in29(_29), .in30(_30), .in31(_31), .out(RD2), .sel(A2));  // open: en
endmodule

module EXT (
  input  [15:0] In,
  input  ExtOp,
  output [31:0] Out
);

  wire [31:0] bit_extender_1_out, bit_extender_2_out;

  assign bit_extender_1_out = {{16{In[15]}}, In};  // Bit_Extender bit_extender_1
  assign bit_extender_2_out = {{16{1'b0}}, In};  // Bit_Extender bit_extender_2
  Multiplexer #(.width(32)) multiplexer_1 (
    .in0(bit_extender_1_out), .in1(bit_extender_2_out), .out(Out), .sel(ExtOp));  // open: en
endmodule

module Splitter (
  input  [31:0] Instr,
  output [5:0] Func,
  output [15:0] Imm16,
  output [4:0] _15_11,
  output [4:0] _20_16,
  output [4:0] _25_21,
  output [5:0] OPCode,
  output [25:0] _25_0
);


  assign _15_11 = Instr[15:11];
  assign _20_16 = Instr[20:16];
  assign _25_0 = Instr[25:0];
  assign _25_21 = Instr[25:21];
  assign Func = Instr[5:0];
  assign Imm16 = Instr[15:0];
  assign OPCode = Instr[31:26];
endmodule

module ALU (
  input  [31:0] A,
  input  [31:0] B,
  input  [2:0] ALUCtrl,
  output [31:0] Result,
  output Zero
);

  wire or_2_out;
  wire [0:0] Compare;
  wire [31:0] Add, And, Or, Sub;

  assign And = A & B;  // AND_Gate and_1, 32 bits wide
  assign Or = A | B;  // OR_Gate or_1, 32 bits wide
  Adder #(.width(32)) adder_1 (.a(A), .b(B), .out(Add));  // open: cin, cout
  Subtractor #(.width(32)) subtractor_1 (.a(A), .b(B), .out(Sub));  // open: bin, bout
  Comparator #(.width(32)) comparator_1 (.a(A), .b(B), .gt(Compare[0]));  // open: eq, lt
  Multiplexer #(.select(3), .width(32)) multiplexer_1 (
    .in0(And), .in1(Or), .in2(Add), .in3(Sub), .in5({{31{1'b0}}, Compare[0]}), .out(Result), .sel(ALUCtrl));  // open: in4, in6, in7, en
  or or_2 (or_2_out, Sub[0], Sub[1], Sub[2], Sub[3], Sub[4], Sub[5], Sub[6], Sub[7], Sub[8], Sub[9], Sub[10], Sub[11], Sub[12], Sub[13], Sub[14], Sub[15], Sub[17], Sub[18], Sub[19], Sub[20], Sub[21], Sub[22], Sub[23], Sub[24], Sub[25], Sub[26], Sub[27], Sub[28], Sub[29], Sub[30], Sub[31], Sub[16]);
  not not_1 (Zero, or_2_out);

  // Other names for the same wires on the sheet: ctrl[2:0] = ALUCtrl
endmodule

module Ctrl (
  input  [5:0] Op,
  output [1:0] RegDst,
  output ALUSrc,
  output RegWrite,
  output MemWrite,
  output [1:0] MemToReg,
  output EXTOp,
  output Branch,
  output Jump,
  output [2:0] ALUOp
);

  wire not_1_out, not_2_out, not_3_out, not_4_out, not_5_out, not_6_out;

  not not_1 (not_1_out, Op[5]);
  not not_2 (not_2_out, Op[3]);
  not not_3 (not_3_out, Op[4]);
  not not_4 (not_4_out, Op[2]);
  not not_5 (not_5_out, Op[0]);
  not not_6 (not_6_out, Op[1]);
  and R (RegDst[0], not_1_out, not_3_out, not_2_out, not_4_out, not_6_out, not_5_out);
  and lw (MemToReg[0], Op[5], not_3_out, not_2_out, not_4_out, Op[1], Op[0]);
  and sw (MemWrite, Op[5], not_3_out, Op[3], not_4_out, Op[1], Op[0]);
  and beq (Branch, not_1_out, not_3_out, not_2_out, Op[2], not_6_out, not_5_out);
  and lui (MemToReg[1], not_1_out, not_3_out, Op[3], Op[2], Op[1], Op[0]);
  and ori (ALUOp[2], not_1_out, not_3_out, Op[3], Op[2], not_6_out, Op[0]);
  and j (Jump, not_1_out, not_3_out, not_2_out, not_4_out, Op[1], not_5_out);
  and jal (RegDst[1], not_1_out, not_3_out, not_2_out, not_4_out, Op[1], Op[0]);
  or or_1 (ALUSrc, MemWrite, MemToReg[0], ALUOp[2]);
  or or_2 (RegWrite, RegDst[0], MemToReg[0], RegDst[1], MemToReg[1], ALUOp[2]);
  or or_3 (ALUOp[1], Branch, MemToReg[1], RegDst[1], ALUOp[2], Jump);
  or or_4 (ALUOp[0], MemToReg[1], MemToReg[0], MemWrite, ALUOp[2], Jump, RegDst[1]);

  assign EXTOp = ALUOp[2];
endmodule

module DM (
  input  Clk,
  input  Reset,
  input  MemWrite,
  input  [4:0] A,
  input  [31:0] WD,
  output [31:0] RD
);

  RAM #(.addrWidth(5), .dataWidth(32), .bus("separate")) ram_1 (
    .addr(A), .din(WD), .data(RD), .str(MemWrite), .clk(Clk), .clr(Reset));  // open: sel, ld

  // Other names for the same wires on the sheet: mw = MemWrite
endmodule

module LeftShift2 (
  input  [31:0] in_1,
  output [31:0] out_2
);

  Shifter #(.width(32)) shifter_1 (.in(in_1), .\dist (5'b00010), .out(out_2));
endmodule

module IFU (
  input  Clk,
  input  Reset,
  input  [31:0] next_PC,
  output [31:0] Instr,
  output [31:0] PC
);

  Register #(.width(32)) u_PC (.D(next_PC), .Q(PC), .clk(Clk), .clr(Reset));  // open: en
  ROM #(.addrWidth(5), .dataWidth(32)) rom_1 (.addr(PC[6:2]), .data(Instr));  // open: sel

  // Notes on the sheet:
  //   contents of rom_1 (hex, n*v repeats v):
  //   5*0 868020 878820 e79020 34080000 ad040000 ad050004 ad060008 ad07000c ad100010 ad110014 ad120018
  //   8d040000 8d05000c ad04001c ad050020 34040001 34050002 34060001 10850001 10860001 ad040024 ad050028
  //   1109fffe 1000ffff
endmodule

module ALUCtrl (
  input  [2:0] ALUOp,
  input  [5:0] Func,
  output [2:0] ALUCtr
);

  wire addu_out, beq_out, jr_out, not_1_out, not_2_out, not_3_out, not_4_out, not_5_out, not_6_out,
       not_7_out, not_8_out, not_9_out, ori_out, subu_out, sw_lw_out;

  not not_1 (not_1_out, ALUOp[2]);
  not not_2 (not_2_out, ALUOp[0]);
  not not_3 (not_3_out, ALUOp[1]);
  not not_4 (not_4_out, Func[5]);
  not not_5 (not_5_out, Func[4]);
  not not_6 (not_6_out, Func[3]);
  not not_7 (not_7_out, Func[2]);
  not not_8 (not_8_out, Func[1]);
  not not_9 (not_9_out, Func[0]);
  and sw_lw (sw_lw_out, not_1_out, not_3_out, ALUOp[0]);
  and beq (beq_out, not_1_out, ALUOp[1], not_2_out);
  and lui_j_jal (ALUCtr[2], not_1_out, ALUOp[1], ALUOp[0]);
  and ori (ori_out, ALUOp[2], ALUOp[1], ALUOp[0]);
  and addu (addu_out, not_1_out, not_3_out, not_2_out, Func[5], not_5_out, not_6_out, not_7_out, not_8_out, not_9_out);
  and subu (subu_out, not_1_out, not_3_out, not_2_out, Func[5], not_5_out, not_6_out, not_7_out, Func[1], not_9_out);
  and jr (jr_out, not_1_out, not_3_out, not_2_out, not_4_out, not_5_out, Func[3], not_7_out, not_8_out, not_9_out);
  or or_1 (ALUCtr[1], ALUCtr[2], sw_lw_out, beq_out, addu_out, subu_out, jr_out);
  or or_2 (ALUCtr[0], beq_out, ALUCtr[2], jr_out, ori_out, subu_out);
endmodule

module LeftShift16 (
  input  [31:0] in_1,
  output [31:0] out_2
);

  Shifter #(.width(32)) shifter_1 (.in(in_1), .\dist (5'b10000), .out(out_2));
endmodule
