// Logisim project Logisim_1Bitswap.circ as structural Verilog: 1 circuit, main circuit swap
module swap (
  input  I1,
  input  I2,
  input  S,
  output O1,
  output O2
);

  wire and_1_out, and_2_out, and_3_out, and_4_out, not_1_out;

  not not_1 (not_1_out, S);
  and and_1 (and_1_out, S, I2);
  and and_2 (and_2_out, S, I1);
  and and_3 (and_3_out, I1, not_1_out);
  and and_4 (and_4_out, not_1_out, I2);
  or or_1 (O1, and_3_out, and_1_out);
  or or_2 (O2, and_4_out, and_2_out);
endmodule
