// Logisim project Logisim_4BitSort.circ as structural Verilog: 5 circuits, main circuit 4bit_sort
module _4bit_sort (
  input  [3:0] A,
  input  [3:0] B,
  input  [3:0] C,
  input  [3:0] D,
  output [3:0] _1,
  output [3:0] _2,
  output [3:0] _3,
  output [3:0] _4
);

  wire [3:0] n4bit_bubble_sort_1_a_2, n4bit_bubble_sort_1_b_2, n4bit_bubble_sort_1_c_2,
       n4bit_bubble_sort_1_d_2, n4bit_bubble_sort_2_a_2, n4bit_bubble_sort_2_b_2, n4bit_bubble_sort_2_c_2,
       n4bit_bubble_sort_2_d_2, n4bit_bubble_sort_3_a_2, n4bit_bubble_sort_3_b_2, n4bit_bubble_sort_3_c_2,
       n4bit_bubble_sort_3_d_2;

  _4bit_bubble_sort u_4bit_bubble_sort_1 (
    .A(A), .B(B), .C(C), .D(D), .A_2(n4bit_bubble_sort_1_a_2), .B_2(n4bit_bubble_sort_1_b_2),
    .C_2(n4bit_bubble_sort_1_c_2), .D_2(n4bit_bubble_sort_1_d_2));
  _4bit_bubble_sort u_4bit_bubble_sort_2 (
    .A(n4bit_bubble_sort_1_a_2), .B(n4bit_bubble_sort_1_b_2), .C(n4bit_bubble_sort_1_c_2),
    .D(n4bit_bubble_sort_1_d_2), .A_2(n4bit_bubble_sort_2_a_2), .B_2(n4bit_bubble_sort_2_b_2),
    .C_2(n4bit_bubble_sort_2_c_2), .D_2(n4bit_bubble_sort_2_d_2));
  _4bit_bubble_sort u_4bit_bubble_sort_3 (
    .A(n4bit_bubble_sort_2_a_2), .B(n4bit_bubble_sort_2_b_2), .C(n4bit_bubble_sort_2_c_2),
    .D(n4bit_bubble_sort_2_d_2), .A_2(n4bit_bubble_sort_3_a_2), .B_2(n4bit_bubble_sort_3_b_2),
    .C_2(n4bit_bubble_sort_3_c_2), .D_2(n4bit_bubble_sort_3_d_2));
  _4bit_bubble_sort u_4bit_bubble_sort_4 (
    .A(n4bit_bubble_sort_3_a_2), .B(n4bit_bubble_sort_3_b_2), .C(n4bit_bubble_sort_3_c_2),
    .D(n4bit_bubble_sort_3_d_2), .A_2(_1), .B_2(_2), .C_2(_3), .D_2(_4));
endmodule

module _1bit_swap (
  input  I1,
  input  I2,
  input  S,
  output O1,
  output O2
);

  wire and_1_out, and_2_out, and_3_out, and_4_out, not_1_out, not_2_out;

  not not_1 (not_1_out, S);
  not not_2 (not_2_out, S);
  and and_1 (and_1_out, I2, S);
  and and_2 (and_2_out, I1, not_1_out);
  and and_3 (and_3_out, I2, not_2_out);
  and and_4 (and_4_out, I1, S);
  or or_1 (O1, and_1_out, and_2_out);
  or or_2 (O2, and_3_out, and_4_out);
endmodule

module _4bit_swap (
  input  [3:0] I1,
  input  [3:0] I2,
  input  S,
  output [3:0] O1,
  output [3:0] O2
);

  _1bit_swap u_1bit_swap_1 (.I1(I1[0]), .I2(I2[0]), .S(S), .O1(O1[0]), .O2(O2[0]));
  _1bit_swap u_1bit_swap_2 (.I1(I1[1]), .I2(I2[1]), .S(S), .O1(O1[1]), .O2(O2[1]));
  _1bit_swap u_1bit_swap_3 (.I1(I1[2]), .I2(I2[2]), .S(S), .O1(O1[2]), .O2(O2[2]));
  _1bit_swap u_1bit_swap_4 (.I1(I1[3]), .I2(I2[3]), .S(S), .O1(O1[3]), .O2(O2[3]));
endmodule

module _4bit_sort_2 (
  input  [3:0] I1,
  input  [3:0] I2,
  output [3:0] O1,
  output [3:0] O2
);

  wire comparator_1_gt;

  Comparator #(.width(4), .mode("unsigned")) comparator_1 (.a(I1), .b(I2), .gt(comparator_1_gt));  // open: eq, lt
  _4bit_swap u_4bit_swap_1 (.I1(I1), .I2(I2), .S(comparator_1_gt), .O1(O1), .O2(O2));
endmodule

module _4bit_bubble_sort (
  input  [3:0] A,
  input  [3:0] B,
  input  [3:0] C,
  input  [3:0] D,
  output [3:0] A_2,
  output [3:0] B_2,
  output [3:0] C_2,
  output [3:0] D_2
);

  wire [3:0] n4bit_sort_2_1_o2, n4bit_sort_2_2_o2;

  _4bit_sort_2 u_4bit_sort_2_1 (.I1(A), .I2(B), .O1(A_2), .O2(n4bit_sort_2_1_o2));
  _4bit_sort_2 u_4bit_sort_2_2 (.I1(n4bit_sort_2_1_o2), .I2(C), .O1(B_2), .O2(n4bit_sort_2_2_o2));
  _4bit_sort_2 u_4bit_sort_2_3 (.I1(n4bit_sort_2_2_o2), .I2(D), .O1(C_2), .O2(D_2));
endmodule
