// Logisim project Logisim_fibonacci.circ as structural Verilog: 2 circuits, main circuit main
module main (
  input  [2:0] n,
  output [3:0] nth
);

  wire clock_1_out, comparator_1_lt;
  wire [3:0] bit_extender_1_out, counter_1_q, fibonacci_1_out_3;

  Clock clock_1 (.out(clock_1_out));
  assign bit_extender_1_out = {{1{1'b0}}, n};  // Bit_Extender bit_extender_1
  Counter #(.width(4), .max('hf), .ongoal("stay")) counter_1 (
    .Q(counter_1_q), .clk(clock_1_out), .clr(1'b0));  // open: load, D, count, carry
  Comparator #(.width(4), .mode("unsigned")) comparator_1 (
    .a(bit_extender_1_out), .b(counter_1_q), .lt(comparator_1_lt));  // open: gt, eq
  fibonacci fibonacci_1 (.reset(1'b0), .output_signal(comparator_1_lt), .out_3(fibonacci_1_out_3));
  Multiplexer #(.width(4)) multiplexer_1 (
    .in0(4'b0000), .in1(fibonacci_1_out_3), .out(nth), .sel(comparator_1_lt));  // open: en
endmodule

module fibonacci (
  input  reset,
  input  output_signal,
  output [3:0] out_3
);

  wire clk_out, counter_1_q, not_1_out, undriven;
  wire [3:0] adder_1_out, multiplexer_1_out, pre_q;

  Clock clk (.out(clk_out));
  Adder #(.width(4)) adder_1 (.a(out_3), .b(pre_q), .out(adder_1_out));  // open: cin, cout
  Counter #(.width(1), .max('h1), .ongoal("stay")) counter_1 (
    .Q(counter_1_q), .clk(clk_out), .clr(reset));  // open: load, D, count, carry
  not not_1 (not_1_out, output_signal);
  Multiplexer #(.width(4)) multiplexer_1 (
    .in0(4'b0001), .in1(out_3), .out(multiplexer_1_out), .sel(counter_1_q), .en(undriven));
  Register #(.width(4)) now (.D(adder_1_out), .en(not_1_out), .Q(out_3), .clk(clk_out), .clr(reset));
  Register #(.width(4)) pre (.D(multiplexer_1_out), .en(not_1_out), .Q(pre_q), .clk(clk_out), .clr(reset));
endmodule
