// Logisim project Logisim_fibonacci2.circ as structural Verilog: 8 circuits, main circuit main
module main (
  input  [31:0] N,
  output [31:0] Nth
);

  wire counter_lowest_bit, counter_stop_signal, not_1_out;
  wire [31:0] calculator_out_3;

  counter counter (.N(N), .lowest_bit(counter_lowest_bit), .stop_signal(counter_stop_signal));
  not not_1 (not_1_out, counter_stop_signal);
  calculator calculator (.lowest_bit(counter_lowest_bit), .stop_signal(not_1_out), .out_3(calculator_out_3));
  Multiplexer #(.width(32), .enable("false")) multiplexer_1 (
    .in0(calculator_out_3), .in1({32{1'b0}}), .out(Nth), .sel(not_1_out));
endmodule

module calculator (
  input  lowest_bit,
  input  stop_signal,
  output [31:0] out_3
);

  wire clock_1_out, init_signal;
  wire [31:0] matrix1_1_out_1, matrix1_1_out_2, matrix1_1_out_3, matrix1_1_out_4, matrix1_2_out_1,
       matrix1_2_out_2, matrix1_2_out_3, matrix1_2_out_4, matrix2_1_out_1, matrix2_1_out_2, matrix2_1_out_3,
       matrix2_1_out_4, matrix_multiple_1_r00, matrix_multiple_1_r01, matrix_multiple_1_r10,
       matrix_multiple_1_r11, matrix_multiple_2_r00, matrix_multiple_2_r01, matrix_multiple_2_r10,
       matrix_multiple_2_r11, matrix_mux_1_r00, matrix_mux_1_r01, matrix_mux_1_r10, matrix_mux_1_r11,
       matrix_mux_2_r00, matrix_mux_2_r01, matrix_mux_2_r10, matrix_mux_2_r11, matrix_mux_3_r00,
       matrix_mux_3_r01, matrix_mux_3_r10, matrix_mux_3_r11, now00, now01, now10, now11, res00, res10, res11;

  Clock clock_1 (.out(clock_1_out));
  Counter #(.width(1), .max('h1), .ongoal("stay")) counter_1 (
    .Q(init_signal), .clk(clock_1_out));  // open: load, D, count, carry, clr
  matrix1 matrix1_1 (
    .out_1(matrix1_1_out_1), .out_2(matrix1_1_out_2), .out_3(matrix1_1_out_3), .out_4(matrix1_1_out_4));
  matrix_mux matrix_mux_1 (
    .A00(matrix1_1_out_1), .A01(matrix1_1_out_2), .A10(matrix1_1_out_3), .A11(matrix1_1_out_4), .B00(now00),
    .B01(now01), .B10(now10), .B11(now11), .in_9(lowest_bit), .R00(matrix_mux_1_r00), .R01(matrix_mux_1_r01),
    .R10(matrix_mux_1_r10), .R11(matrix_mux_1_r11));
  matrix_multiple matrix_multiple_1 (
    .A00(now00), .A01(now01), .A10(now10), .A11(now11), .B00(now00), .B01(now01), .B10(now10), .B11(now11),
    .R00(matrix_multiple_1_r00), .R01(matrix_multiple_1_r01), .R10(matrix_multiple_1_r10),
    .R11(matrix_multiple_1_r11));
  matrix1 matrix1_2 (
    .out_1(matrix1_2_out_1), .out_2(matrix1_2_out_2), .out_3(matrix1_2_out_3), .out_4(matrix1_2_out_4));
  matrix_multiple matrix_multiple_2 (
    .A00(res00), .A01(out_3), .A10(res10), .A11(res11), .B00(matrix_mux_1_r00), .B01(matrix_mux_1_r01),
    .B10(matrix_mux_1_r10), .B11(matrix_mux_1_r11), .R00(matrix_multiple_2_r00), .R01(matrix_multiple_2_r01),
    .R10(matrix_multiple_2_r10), .R11(matrix_multiple_2_r11));
  matrix2 matrix2_1 (
    .out_1(matrix2_1_out_1), .out_2(matrix2_1_out_2), .out_3(matrix2_1_out_3), .out_4(matrix2_1_out_4));
  matrix_mux matrix_mux_2 (
    .A00(matrix1_2_out_1), .A01(matrix1_2_out_2), .A10(matrix1_2_out_3), .A11(matrix1_2_out_4),
    .B00(matrix_multiple_2_r00), .B01(matrix_multiple_2_r01), .B10(matrix_multiple_2_r10),
    .B11(matrix_multiple_2_r11), .in_9(init_signal), .R00(matrix_mux_2_r00), .R01(matrix_mux_2_r01),
    .R10(matrix_mux_2_r10), .R11(matrix_mux_2_r11));
  matrix_mux matrix_mux_3 (
    .A00(matrix2_1_out_1), .A01(matrix2_1_out_2), .A10(matrix2_1_out_3), .A11(matrix2_1_out_4),
    .B00(matrix_multiple_1_r00), .B01(matrix_multiple_1_r01), .B10(matrix_multiple_1_r10),
    .B11(matrix_multiple_1_r11), .in_9(init_signal), .R00(matrix_mux_3_r00), .R01(matrix_mux_3_r01),
    .R10(matrix_mux_3_r10), .R11(matrix_mux_3_r11));
  matrix_register matrix_register_1 (
    .in_1(matrix_mux_2_r00), .in_2(matrix_mux_2_r01), .in_3(matrix_mux_2_r10), .in_4(matrix_mux_2_r11),
    .out_6(res00), .out_7(out_3), .out_8(res10), .out_9(res11), .stop_signal(stop_signal));
  matrix_register matrix_register_2 (
    .in_1(matrix_mux_3_r00), .in_2(matrix_mux_3_r01), .in_3(matrix_mux_3_r10), .in_4(matrix_mux_3_r11),
    .out_6(now00), .out_7(now01), .out_8(now10), .out_9(now11), .stop_signal(stop_signal));

  // Other names for the same wires on the sheet: res01[31:0] = out_3
endmodule

module counter (
  input  [31:0] N,
  output lowest_bit,
  output stop_signal
);

  wire clk, comparator_1_eq, init_signal, not_1_out;
  wire [31:0] multiplexer_1_out, N_t, shifter_1_out;

  Counter #(.width(1), .max('h1), .ongoal("stay")) counter_1 (
    .Q(init_signal), .clk(clk));  // open: load, D, count, carry, clr
  Clock clock_1 (.out(clk));
  Shifter #(.width(32), .shift("lr")) shifter_1 (.in(N_t), .\dist (5'b00001), .out(shifter_1_out));
  not not_1 (not_1_out, stop_signal);
  Multiplexer #(.width(32), .enable("false")) multiplexer_1 (
    .in0(N), .in1(shifter_1_out), .out(multiplexer_1_out), .sel(init_signal));
  Register #(.width(32)) register_1 (.D(multiplexer_1_out), .en(not_1_out), .Q(N_t), .clk(clk));  // open: clr
  Bit_Extender #(.in_width(32), .out_width(1)) bit_extender_1 (.in(N_t), .out(lowest_bit));
  Comparator #(.width(32), .mode("unsigned")) comparator_1 (
    .a(N_t), .b({32{1'b0}}), .eq(comparator_1_eq));  // open: gt, lt
  Multiplexer #(.enable("false")) multiplexer_2 (
    .in0(1'b0), .in1(comparator_1_eq), .out(stop_signal), .sel(init_signal));
endmodule

module matrix_multiple (
  input  [31:0] A00,
  input  [31:0] A01,
  input  [31:0] A10,
  input  [31:0] A11,
  input  [31:0] B00,
  input  [31:0] B01,
  input  [31:0] B10,
  input  [31:0] B11,
  output [31:0] R00,
  output [31:0] R01,
  output [31:0] R10,
  output [31:0] R11
);

  wire [31:0] multiplier_1_out, multiplier_2_out, multiplier_3_out, multiplier_4_out, multiplier_5_out,
       multiplier_6_out, multiplier_7_out, multiplier_8_out;

  Multiplier #(.width(32)) multiplier_1 (.a(A00), .b(B00), .out(multiplier_1_out));  // open: cin, cout
  Multiplier #(.width(32)) multiplier_2 (.a(A01), .b(B10), .out(multiplier_2_out));  // open: cin, cout
  Multiplier #(.width(32)) multiplier_3 (.a(A00), .b(B01), .out(multiplier_3_out));  // open: cin, cout
  Multiplier #(.width(32)) multiplier_4 (.a(A01), .b(B11), .out(multiplier_4_out));  // open: cin, cout
  Multiplier #(.width(32)) multiplier_5 (.a(A10), .b(B00), .out(multiplier_5_out));  // open: cin, cout
  Multiplier #(.width(32)) multiplier_6 (.a(A11), .b(B10), .out(multiplier_6_out));  // open: cin, cout
  Multiplier #(.width(32)) multiplier_7 (.a(A10), .b(B01), .out(multiplier_7_out));  // open: cin, cout
  Multiplier #(.width(32)) multiplier_8 (.a(A11), .b(B11), .out(multiplier_8_out));  // open: cin, cout
  Adder #(.width(32)) adder_1 (.a(multiplier_1_out), .b(multiplier_2_out), .out(R00));  // open: cin, cout
  Adder #(.width(32)) adder_2 (.a(multiplier_3_out), .b(multiplier_4_out), .out(R01));  // open: cin, cout
  Adder #(.width(32)) adder_3 (.a(multiplier_5_out), .b(multiplier_6_out), .out(R10));  // open: cin, cout
  Adder #(.width(32)) adder_4 (.a(multiplier_7_out), .b(multiplier_8_out), .out(R11));  // open: cin, cout
endmodule

module matrix_mux (
  input  [31:0] A00,
  input  [31:0] A01,
  input  [31:0] A10,
  input  [31:0] A11,
  input  [31:0] B00,
  input  [31:0] B01,
  input  [31:0] B10,
  input  [31:0] B11,
  input  in_9,
  output [31:0] R00,
  output [31:0] R01,
  output [31:0] R10,
  output [31:0] R11
);

  Multiplexer #(.width(32), .enable("false")) multiplexer_1 (.in0(A00), .in1(B00), .out(R00), .sel(in_9));
  Multiplexer #(.width(32), .enable("false")) multiplexer_2 (.in0(A01), .in1(B01), .out(R01), .sel(in_9));
  Multiplexer #(.width(32), .enable("false")) multiplexer_3 (.in0(A10), .in1(B10), .out(R10), .sel(in_9));
  Multiplexer #(.width(32), .enable("false")) multiplexer_4 (.in0(A11), .in1(B11), .out(R11), .sel(in_9));

  // Other names for the same wires on the sheet: select = in_9
endmodule

module matrix1 (
  output [31:0] out_1,
  output [31:0] out_2,
  output [31:0] out_3,
  output [31:0] out_4
);


  assign out_1 = 32'h1;
  assign out_2 = {32{1'b0}};
  assign out_3 = {32{1'b0}};
  assign out_4 = 32'h1;
endmodule

module matrix2 (
  output [31:0] out_1,
  output [31:0] out_2,
  output [31:0] out_3,
  output [31:0] out_4
);


  assign out_1 = 32'h1;
  assign out_2 = 32'h1;
  assign out_3 = 32'h1;
  assign out_4 = {32{1'b0}};
endmodule

module matrix_register (
  input  [31:0] in_1,
  input  [31:0] in_2,
  input  [31:0] in_3,
  input  [31:0] in_4,
  input  stop_signal,
  output [31:0] out_6,
  output [31:0] out_7,
  output [31:0] out_8,
  output [31:0] out_9
);

  wire clk;

  Clock clock_1 (.out(clk));
  Register #(.width(32)) register_1 (.D(in_1), .en(stop_signal), .Q(out_6), .clk(clk));  // open: clr
  Register #(.width(32)) register_2 (.D(in_2), .en(stop_signal), .Q(out_7), .clk(clk));  // open: clr
  Register #(.width(32)) register_3 (.D(in_3), .en(stop_signal), .Q(out_8), .clk(clk));  // open: clr
  Register #(.width(32)) register_4 (.D(in_4), .en(stop_signal), .Q(out_9), .clk(clk));  // open: clr

  // Other names for the same wires on the sheet: ss = stop_signal
endmodule
