// Logisim project Logisim_mod5(false).circ as structural Verilog: 6 circuits, main circuit mod5
module mod5 (
  input  In,
  output S0,
  output S1,
  output S2,
  output S3,
  output S4
);

  wire clock_1_out;
  wire [4:0] s0_1_s0_2;

  s0 s0_1 (.in(In), .s0(In), .s1(S1), .s2(S2), .s3(S3), .s4(S4), .s0_2(s0_1_s0_2[0]));
  s1 s1_1 (.in(In), .s0(In), .s1(S1), .s2(S2), .s3(S3), .s4(S4), .s1_2(s0_1_s0_2[1]));
  s2 s2_1 (.in(In), .s0(In), .s1(S1), .s2(S2), .s3(S3), .s4(S4), .s1_2(s0_1_s0_2[2]));
  s3 s3_1 (.in(In), .s0(In), .s1(S1), .s2(S2), .s3(S3), .s4(S4), .s1_2(s0_1_s0_2[3]));
  s4 s4_1 (.in(In), .s0(In), .s1(S1), .s2(S2), .s3(S3), .s4(S4), .s1_2(s0_1_s0_2[4]));
  Register #(.width(5)) register_1 (
    .D(s0_1_s0_2), .Q({S4, S3, S2, S1, In}), .clk(clock_1_out), .clr(1'b0));  // open: en
  Clock clock_1 (.out(clock_1_out));

  assign S0 = In;
endmodule

module s0 (
  input  in,
  input  s0,
  input  s1,
  input  s2,
  input  s3,
  input  s4,
  output s0_2
);

  wire and_1_out, and_2_out, not_1_out, not_2_out, not_3_out, not_4_out, not_5_out, not_6_out, not_7_out,
       not_8_out, not_9_out;

  not not_1 (not_1_out, s1);
  not not_2 (not_2_out, s2);
  not not_3 (not_3_out, s3);
  not not_4 (not_4_out, s4);
  not not_5 (not_5_out, in);
  not not_6 (not_6_out, s0);
  not not_7 (not_7_out, s1);
  not not_8 (not_8_out, s3);
  not not_9 (not_9_out, s4);
  and and_1 (and_1_out, s0, not_1_out, not_2_out, not_3_out, not_4_out, not_5_out);
  and and_2 (and_2_out, not_6_out, not_7_out, s2, not_8_out, not_9_out, in);
  or or_1 (s0_2, and_1_out, and_2_out);
endmodule

module s1 (
  input  in,
  input  s0,
  input  s1,
  input  s2,
  input  s3,
  input  s4,
  output s1_2
);

  wire and_1_out, and_2_out, not_1_out, not_2_out, not_3_out, not_4_out, not_5_out, not_6_out, not_7_out,
       not_8_out, not_9_out;

  not not_1 (not_1_out, s1);
  not not_2 (not_2_out, s2);
  not not_3 (not_3_out, s3);
  not not_4 (not_4_out, s4);
  not not_5 (not_5_out, s0);
  not not_6 (not_6_out, s1);
  not not_7 (not_7_out, s2);
  not not_8 (not_8_out, s4);
  not not_9 (not_9_out, in);
  and and_1 (and_1_out, s0, not_1_out, not_2_out, not_3_out, not_4_out, in);
  and and_2 (and_2_out, not_5_out, not_6_out, not_7_out, s3, not_8_out, not_9_out);
  or or_1 (s1_2, and_1_out, and_2_out);
endmodule

module s2 (
  input  in,
  input  s0,
  input  s1,
  input  s2,
  input  s3,
  input  s4,
  output s1_2
);

  wire and_1_out, and_2_out, not_1_out, not_2_out, not_3_out, not_4_out, not_5_out, not_6_out, not_7_out,
       not_8_out, not_9_out;

  not not_1 (not_1_out, s1);
  not not_2 (not_2_out, s2);
  not not_3 (not_3_out, s3);
  not not_4 (not_4_out, s4);
  not not_5 (not_5_out, s0);
  not not_6 (not_6_out, s1);
  not not_7 (not_7_out, s2);
  not not_8 (not_8_out, s4);
  not not_9 (not_9_out, in);
  and and_1 (and_1_out, s0, not_1_out, not_2_out, not_3_out, not_4_out, in);
  and and_2 (and_2_out, not_5_out, not_6_out, not_7_out, s3, not_8_out, not_9_out);
  or or_1 (s1_2, and_1_out, and_2_out);
endmodule

module s3 (
  input  in,
  input  s0,
  input  s1,
  input  s2,
  input  s3,
  input  s4,
  output s1_2
);

  wire and_1_out, and_2_out, not_1_out, not_2_out, not_3_out, not_4_out, not_5_out, not_6_out, not_7_out,
       not_8_out, not_9_out;

  not not_1 (not_1_out, s1);
  not not_2 (not_2_out, s2);
  not not_3 (not_3_out, s3);
  not not_4 (not_4_out, s4);
  not not_5 (not_5_out, s0);
  not not_6 (not_6_out, s1);
  not not_7 (not_7_out, s2);
  not not_8 (not_8_out, s4);
  not not_9 (not_9_out, in);
  and and_1 (and_1_out, s0, not_1_out, not_2_out, not_3_out, not_4_out, in);
  and and_2 (and_2_out, not_5_out, not_6_out, not_7_out, s3, not_8_out, not_9_out);
  or or_1 (s1_2, and_1_out, and_2_out);
endmodule

module s4 (
  input  in,
  input  s0,
  input  s1,
  input  s2,
  input  s3,
  input  s4,
  output s1_2
);

  wire and_1_out, and_2_out, not_1_out, not_2_out, not_3_out, not_4_out, not_5_out, not_6_out, not_7_out,
       not_8_out, not_9_out;

  not not_1 (not_1_out, s1);
  not not_2 (not_2_out, s2);
  not not_3 (not_3_out, s3);
  not not_4 (not_4_out, s4);
  not not_5 (not_5_out, s0);
  not not_6 (not_6_out, s1);
  not not_7 (not_7_out, s2);
  not not_8 (not_8_out, s4);
  not not_9 (not_9_out, in);
  and and_1 (and_1_out, s0, not_1_out, not_2_out, not_3_out, not_4_out, in);
  and and_2 (and_2_out, not_5_out, not_6_out, not_7_out, s3, not_8_out, not_9_out);
  or or_1 (s1_2, and_1_out, and_2_out);
endmodule
