// Logisim project Logisim_mod5.circ as structural Verilog: 3 circuits, main circuit mod5
module mod5 (
  input  In,
  output S0,
  output S1,
  output S2,
  output S3,
  output S4
);

  wire clock_1_out;
  wire [1:0] register_1_q, trans_1_out_3;

  trans trans_1 (.in(In), .in_2(register_1_q), .out_3(trans_1_out_3));
  Clock clock_1 (.out(clock_1_out));
  Register #(.width(2)) register_1 (.D(trans_1_out_3), .Q(register_1_q), .clk(clock_1_out), .clr(1'b0));  // open: en
  \output  output_1 (.c1(register_1_q[0]), .c2(register_1_q[1]), .in(In), .s1(S1), .s2(S2), .s3(S3), .s4(S4));

  assign S0 = 1'b0;
endmodule

module \output  (
  input  c1,
  input  c2,
  input  in,
  output s1,
  output s2,
  output s3,
  output s4
);

  wire and_1_out, and_2_out, and_3_out, and_4_out, and_5_out, and_6_out, and_7_out, and_8_out, not_1_out,
       not_2_out, not_3_out, not_4_out, not_5_out, not_6_out, not_7_out, not_8_out, not_9_out, not_10_out,
       not_11_out, not_12_out;

  not not_1 (not_1_out, c1);
  not not_2 (not_2_out, c2);
  not not_3 (not_3_out, in);
  not not_4 (not_4_out, in);
  not not_5 (not_5_out, c1);
  not not_6 (not_6_out, c2);
  not not_7 (not_7_out, c1);
  not not_8 (not_8_out, c2);
  not not_9 (not_9_out, c1);
  not not_10 (not_10_out, in);
  not not_11 (not_11_out, c2);
  not not_12 (not_12_out, in);
  and and_1 (and_1_out, not_1_out, not_2_out, not_3_out);
  and and_2 (and_2_out, c1, c2, not_4_out);
  and and_3 (and_3_out, not_5_out, not_6_out, in);
  and and_4 (and_4_out, c1, c2, in);
  and and_5 (and_5_out, not_7_out, c2, in);
  and and_6 (and_6_out, c1, not_8_out, in);
  and and_7 (and_7_out, not_9_out, c2, not_10_out);
  and and_8 (and_8_out, c1, not_11_out, not_12_out);
  or or_1 (s1, and_1_out, and_2_out);
  or or_2 (s2, and_3_out, and_4_out);
  or or_3 (s3, and_5_out, and_6_out);
  or or_4 (s4, and_7_out, and_8_out);
endmodule

module trans (
  input  in,
  input  [1:0] in_2,
  output [1:0] out_3
);

  wire and_1_out, and_2_out, and_3_out, and_4_out, and_5_out, and_6_out, not_1_out, not_2_out, not_3_out,
       not_4_out, not_5_out, not_6_out, not_7_out, not_8_out;

  not not_1 (not_1_out, in_2[1]);
  not not_2 (not_2_out, in_2[0]);
  not not_3 (not_3_out, in);
  not not_4 (not_4_out, in_2[1]);
  not not_5 (not_5_out, in);
  not not_6 (not_6_out, in_2[0]);
  not not_7 (not_7_out, in_2[1]);
  not not_8 (not_8_out, in_2[0]);
  and and_1 (and_1_out, not_1_out, in_2[0]);
  and and_2 (and_2_out, in_2[1], not_2_out);
  and and_3 (and_3_out, not_3_out, not_4_out, in_2[0]);
  and and_4 (and_4_out, not_5_out, in_2[1], not_6_out);
  and and_5 (and_5_out, in, not_7_out, not_8_out);
  and and_6 (and_6_out, in, in_2[1], in_2[0]);
  or or_1 (out_3[1], and_1_out, and_2_out);
  or or_2 (out_3[0], and_3_out, and_4_out, and_5_out, and_6_out);
endmodule
